# Fritzing sketch wiring (saved by Fritzing 0.9.6b)
circuit board: 3.08417cm x 4.17732cm
breadboards: 1

parts:
  R4 = Resistor [tolerance=±5% power=0.25W resistance=1k package=THT]
  Q2 = NPN-Transistor [mpn=2N3904 package="TO92 [THT]"]
  R2 = Resistor [tolerance=±5% power=0.25W resistance=100 package=THT]
  Q1 = PNP-Transistor [mpn=2N3906 package="TO92 [THT]"]
  R1 = Resistor [tolerance=±5% power=0.25W resistance=47k package=THT]
  R3 = Resistor [tolerance=±5% power=0.25W resistance=4.7k package=THT]
  J1 = male pin header, 3 pins [form="♂ (male)"]
  J2 = male pin header, 2 pins [form="♂ (male)"]
  J3 = male pin header, 2 pins [form="♂ (male)"]
  R5 = Resistor [tolerance=±5% power=0.25 resistance=220 package=THT]
  R6 = Resistor [tolerance=±5% power=0.25 resistance=220 package=THT]
  R7 = Resistor [tolerance=±5% power=0.25 resistance=220 package=THT]
  R8 = Resistor [tolerance=±5% power=0.25 resistance=220 package=THT]
  J4 = male pin header, 1 pin [form="♂ (male)"]
  J5 = male pin header, 1 pin [form="♂ (male)"]
  J6 = male pin header, 1 pin [form="♂ (male)"]
  J7 = male pin header, 1 pin [form="♂ (male)"]
  J8 = male pin header, 1 pin [form="♂ (male)"]
  J9 = male pin header, 1 pin [form="♂ (male)"]
  J10 = male pin header, 1 pin [form="♂ (male)"]
  J11 = male pin header, 1 pin [form="♂ (male)"]
  J12 = male pin header, 1 pin [form="♂ (male)"]

nets:
  N1: R4.Pin_0, J2.pin2
  N2: R4.Pin_1, Q2.B
  N3: Q2.E, J1.pin1, J3.pin2, J12.pin1
  N4: Q2.C, R2.Pin_1
  N5: R2.Pin_0, Q1.B, R1.Pin_1
  N6: Q1.E, R1.Pin_0, J3.pin1
  N7: Q1.C, R3.Pin_0, J1.pin2
  N8: R3.Pin_1, J1.pin3, J2.pin1
  N9: R5.Pin_0, J4.pin1
  N10: R5.Pin_1, J8.pin1
  N11: R6.Pin_0, J5.pin1
  N12: R6.Pin_1, J9.pin1
  N13: R7.Pin_0, J6.pin1
  N14: R7.Pin_1, J10.pin1
  N15: R8.Pin_0, J7.pin1
  N16: R8.Pin_1, J11.pin1
